# Fritzing sketch single LED (saved by Fritzing 0.9.2b)
breadboards: 1

parts:
  C1 = Electrolytic Capacitor [capacitance=1µF package="100 mil [THT, electrolytic]"]
  LED2 = RGB LED (com. cathode, rgb) [package="5 mm [THT]"]
  Part1 = Arduino Uno (Rev3)
  R1 = Resistor [tolerance=±5% resistance=220 package=THT]

nets:
  N1: C1.-, LED2.green_anode, Part1.GND
  N2: C1.+, LED2.common_cathode, Part1.5V
  N3: LED2.red_anode, R1.Pin_1
  N4: Part1.D6_PWM, R1.Pin_0
