# Fritzing sketch six LEDs (saved by Fritzing 0.9.2b)
breadboards: 1

parts:
  Part1 = Arduino Uno (Rev3)
  C1 = Electrolytic Capacitor [capacitance=100µF package="100 mil [THT, electrolytic]"]
  R1 = Resistor [tolerance=±5% resistance=220 package=THT]
  LED1 = RGB LED (com. cathode, rgb) [package="5 mm [THT]"]
  LED2 = RGB LED (com. cathode, rgb) [package="5 mm [THT]"]
  LED3 = RGB LED (com. cathode, rgb) [package="5 mm [THT]"]
  LED4 = RGB LED (com. cathode, rgb) [package="5 mm [THT]"]
  LED5 = RGB LED (com. cathode, rgb) [package="5 mm [THT]"]
  LED6 = RGB LED (com. cathode, rgb) [package="5 mm [THT]"]

nets:
  N1: Part1.D6_PWM, R1.Pin_0
  N2: Part1.5V, C1.+, LED1.common_cathode, LED1.green_anode, LED2.common_cathode, LED2.green_anode, LED3.common_cathode, LED3.green_anode, LED4.common_cathode, LED4.green_anode, LED5.common_cathode, LED5.green_anode, LED6.common_cathode, LED6.green_anode
  N3: Part1.GND, C1.-
  N4: R1.Pin_1, LED1.blue_anode
  N5: LED1.red_anode, LED2.blue_anode
  N6: LED2.red_anode, LED3.blue_anode
  N7: LED3.red_anode, LED4.blue_anode
  N8: LED4.red_anode, LED5.blue_anode
  N9: LED5.red_anode, LED6.blue_anode
